// Logisim project hw4part2.circ as structural Verilog: 2 circuits, main circuit One-Hot State Machine
module Tester (
  input  G
);

  wire Clock_out, one_hot_state_machine_1_w, one_hot_state_machine_1_x, one_hot_state_machine_1_y,
       one_hot_state_machine_1_z, Reset_out;

  One_Hot_State_Machine one_hot_state_machine_1 (
    .W(one_hot_state_machine_1_w), .Clock(Clock_out), .Reset(Reset_out), .G(G),
    .X(one_hot_state_machine_1_x), .Y(one_hot_state_machine_1_y), .Z(one_hot_state_machine_1_z));
  Clock Clock (.out(Clock_out));
  LED W (.in(one_hot_state_machine_1_w));
  LED X (.in(one_hot_state_machine_1_x));
  LED Y (.in(one_hot_state_machine_1_y));
  LED Z (.in(one_hot_state_machine_1_z));
  Button Reset (.out(Reset_out));

  // Notes on the sheet:
  //   You can use this to test your circuit.
endmodule

module One_Hot_State_Machine (
  input  G,
  input  Clock,
  input  Reset,
  output W,
  output X,
  output Y,
  output Z
);

  wire and_5_out, and_6_out, and_7_out, and_9_out, and_10_out, L0, L1, L2, L3, L4, L5, L6, M0, N0, P0, P1,
       P2, P3, P4, P5, P6, R0;

  and and_1 (R0, ~G, P0);  // AND_Gate
  and and_2 (L1, G, P0);
  and and_3 (L4, G, P1);
  and and_4 (L2, ~G, P1);  // AND_Gate
  and and_5 (and_5_out, G, P4);
  or or_1 (L5, and_5_out, and_6_out);
  and and_6 (and_6_out, G, P3);
  and and_7 (and_7_out, G, P6);
  or or_2 (L6, and_7_out, P5);
  and and_8 (M0, ~G, P6);  // AND_Gate
  and and_9 (and_9_out, ~G, P3);  // AND_Gate
  and and_10 (and_10_out, ~G, P4);  // AND_Gate
  or or_3 (L3, P2, and_9_out, and_10_out);
  Register #(.width(7)) register_1 (
    .D({L6, L5, L4, L3, L2, L1, L0}), .Q({P6, P5, P4, P3, P2, P1, P0}), .clk(Clock), .clr(Reset));  // open: en
  or or_4 (L0, M0, R0, N0);
  or or_5 (X, P0, P3);
  or or_6 (Z, P2, P4, P5);
  or or_7 (W, P2, P3, P6);
  or or_8 (Y, P3, P5, P6);
  and and_11 (N0, ~P0, ~P1, ~P2, ~P3, ~P4, ~P5, ~P6);  // AND_Gate

  // Other names for the same wires on the sheet: CLK = Clock; RST = Reset

  // Notes on the sheet:
  //   My name is
  //   Susan Roberts
  //   Implement your one-hot state machine circuit here!
  //   and this is my pretty one-hot state machine!
endmodule
