// Logisim project hw4part3.circ as structural Verilog: 2 circuits, main circuit Reduced State Machine
module Tester (
  input  G
);

  wire Clock_out, reduced_state_machine_1_w, reduced_state_machine_1_x, reduced_state_machine_1_y,
       reduced_state_machine_1_z, Reset_out;

  Reduced_State_Machine reduced_state_machine_1 (
    .W(reduced_state_machine_1_w), .Clock(Clock_out), .Reset(Reset_out), .G(G),
    .X(reduced_state_machine_1_x), .Y(reduced_state_machine_1_y), .Z(reduced_state_machine_1_z));
  Clock Clock (.out(Clock_out));
  LED W (.in(reduced_state_machine_1_w));
  LED X (.in(reduced_state_machine_1_x));
  LED Y (.in(reduced_state_machine_1_y));
  LED Z (.in(reduced_state_machine_1_z));
  Button Reset (.out(Reset_out));

  // Notes on the sheet:
  //   You can use this to test your circuit.
endmodule

module Reduced_State_Machine (
  input  G,
  input  Clock,
  input  Reset,
  output W,
  output X,
  output Y,
  output Z
);

  wire and_1_out, and_2_out, and_3_out, and_4_out, and_5_out, and_6_out, and_7_out, and_8_out, and_9_out,
       and_10_out, and_11_out, and_12_out, and_13_out, and_14_out, and_15_out, and_16_out, and_17_out,
       and_18_out, and_19_out, L0, L1, L2, P0, P2;

  and and_1 (and_1_out, ~P0, ~W, ~P2);  // AND_Gate
  and and_2 (and_2_out, P0, W);
  and and_3 (and_3_out, P0, W);
  and and_4 (and_4_out, P0, P2);
  and and_5 (and_5_out, W, P2);
  and and_6 (and_6_out, ~W, P2);  // AND_Gate
  and and_7 (and_7_out, ~P0, W, ~P2);  // AND_Gate
  or or_1 (X, and_1_out, and_2_out);
  or or_2 (Y, and_3_out, and_4_out, and_5_out);
  or or_3 (Z, and_6_out, and_7_out);
  Register #(.width(3)) register_1 (.D({L2, L1, L0}), .Q({P2, W, P0}), .clk(Clock), .clr(Reset));  // open: en
  and and_8 (and_8_out, G, P2);
  and and_9 (and_9_out, P0, P2);
  and and_10 (and_10_out, G, P0);
  and and_11 (and_11_out, G, ~P0, W);  // AND_Gate
  and and_12 (and_12_out, ~G, ~W, P2);  // AND_Gate
  and and_13 (and_13_out, ~G, W, ~P2);  // AND_Gate
  and and_14 (and_14_out, P0, P2);
  and and_15 (and_15_out, ~G, P0);  // AND_Gate
  and and_16 (and_16_out, ~P0, ~W, P2);  // AND_Gate
  and and_17 (and_17_out, G, ~P0, ~W);  // AND_Gate
  and and_18 (and_18_out, P0, W);
  and and_19 (and_19_out, W, ~P2);  // AND_Gate
  or or_4 (L2, and_8_out, and_9_out, and_10_out);
  or or_5 (L1, and_11_out, and_12_out, and_13_out, and_14_out, and_15_out);
  or or_6 (L0, and_16_out, and_17_out, and_18_out, and_19_out);

  // Other names for the same wires on the sheet: P1 = W; CLK = Clock; RST = Reset

  // Notes on the sheet:
  //   Implement your reduced state machine circuit here!
  //   My name is
  //   Susan Roberts
  //   and this is my pretty reduced state machine!
endmodule
