// Logisim project SusanRoberts_HW03.circ as structural Verilog: 8 circuits, main circuit 16 Bit ALU
module _1_Bit_Adder (
  input  A,
  input  B,
  input  C_in,
  output C_out,
  output Out
);

  wire and_1_out, and_2_out, and_3_out, and_4_out, and_5_out, and_6_out, and_7_out, and_8_out;

  and and_1 (and_1_out, ~A, ~B, ~C_in);  // AND_Gate
  and and_2 (and_2_out, ~A, ~B, C_in);  // AND_Gate
  and and_3 (and_3_out, ~A, B, ~C_in);  // AND_Gate
  and and_4 (and_4_out, ~A, B, C_in);  // AND_Gate
  and and_5 (and_5_out, A, ~B, ~C_in);  // AND_Gate
  and and_6 (and_6_out, A, ~B, C_in);  // AND_Gate
  and and_7 (and_7_out, A, B, ~C_in);  // AND_Gate
  and and_8 (and_8_out, A, B, C_in);
  or or_1 (C_out, and_4_out, and_6_out, and_7_out, and_8_out);
  or or_2 (Out, and_8_out, and_2_out, and_3_out, and_5_out);
endmodule

module _4_Bit_Adder (
  input  C_in,
  input  [3:0] B,
  input  [3:0] A,
  output [3:0] Out,
  output C_out
);

  wire n1_bit_adder_2_c_out, n1_bit_adder_3_c_out, n1_bit_adder_4_c_out;

  _1_Bit_Adder u_1_bit_adder_1 (.A(B[3]), .B(A[3]), .C_in(n1_bit_adder_2_c_out), .C_out(C_out), .Out(Out[3]));
  _1_Bit_Adder u_1_bit_adder_2 (
    .A(B[2]), .B(A[2]), .C_in(n1_bit_adder_3_c_out), .C_out(n1_bit_adder_2_c_out), .Out(Out[2]));
  _1_Bit_Adder u_1_bit_adder_3 (
    .A(B[1]), .B(A[1]), .C_in(n1_bit_adder_4_c_out), .C_out(n1_bit_adder_3_c_out), .Out(Out[1]));
  _1_Bit_Adder u_1_bit_adder_4 (.A(B[0]), .B(A[0]), .C_in(C_in), .C_out(n1_bit_adder_4_c_out), .Out(Out[0]));
endmodule

// C_out
module _4_Bit_ALU (
  input  [3:0] A,
  input  C_in_add,
  input  C_in_subt,
  input  [3:0] B,
  input  C_in_inc,
  input  S2,
  input  S1,
  input  S0,
  output C_out_add,
  output C_out_subt,
  output C_out_inc,
  output [3:0] Out
);

  wire [3:0] and_1_out, n4_bit_adder_1_out, n4_bit_adder_2_out, n4_bit_subtractor_1_out, not_1_out, or_1_out,
       xor_1_out;

  _4_Bit_Adder u_4_bit_adder_1 (.Out(n4_bit_adder_1_out), .C_in(C_in_add), .C_out(C_out_add), .B(B), .A(A));
  _4_Bit_Subtractor u_4_bit_subtractor_1 (
    .Out(n4_bit_subtractor_1_out), .A(A), .B(B), .C_out(C_out_subt), .C_in(C_in_subt));
  _4_Bit_Adder u_4_bit_adder_2 (.Out(n4_bit_adder_2_out), .C_in(C_in_inc), .C_out(C_out_inc), .B(4'b0001), .A(A));
  assign not_1_out = ~A;  // NOT_Gate not_1, 4 bits wide
  assign and_1_out = A & B;  // AND_Gate and_1, 4 bits wide
  assign or_1_out = A | B;  // OR_Gate or_1, 4 bits wide
  assign xor_1_out = A ^ B;  // XOR_Gate xor_1, 4 bits wide
  Multiplexer #(.select(3), .width(4), .disabled(0), .enable("false")) multiplexer_1 (
    .in0(n4_bit_adder_1_out), .in1(n4_bit_subtractor_1_out), .in2(n4_bit_adder_2_out), .in3(not_1_out),
    .in4({1'b0, A[3:1]}), .in5(and_1_out), .in6(or_1_out), .in7(xor_1_out), .out(Out), .sel({S2, S1, S0}));

  // Notes on the sheet:
  //   1. Addition
  //   2. Subtraction
  //   3. Increment
  //   4. Negation
  //   5. Bit Shift
  //   6. AND
  //   7. OR
  //   8. XOR
endmodule

module _1_Bit_Subtractor (
  input  C_in,
  input  A,
  input  B,
  output Out,
  output C_out
);

  wire and_1_out, and_2_out, xor_1_out;

  xor xor_1 (xor_1_out, A, B);
  and and_1 (and_1_out, B, ~A);  // AND_Gate
  xor xor_2 (Out, C_in, xor_1_out);
  and and_2 (and_2_out, ~xor_1_out, C_in);  // AND_Gate
  or or_1 (C_out, and_2_out, and_1_out);
endmodule

module _4_Bit_Subtractor (
  input  C_in,
  input  [3:0] A,
  input  [3:0] B,
  output [3:0] Out,
  output C_out
);

  wire n1_bit_subtractor_2_c_out, n1_bit_subtractor_3_c_out, n1_bit_subtractor_4_c_out;

  _1_Bit_Subtractor u_1_bit_subtractor_1 (
    .C_in(n1_bit_subtractor_3_c_out), .A(A[3]), .B(B[3]), .Out(Out[3]), .C_out(C_out));
  _1_Bit_Subtractor u_1_bit_subtractor_2 (
    .C_in(n1_bit_subtractor_4_c_out), .A(A[1]), .B(B[1]), .Out(Out[1]), .C_out(n1_bit_subtractor_2_c_out));
  _1_Bit_Subtractor u_1_bit_subtractor_3 (
    .C_in(n1_bit_subtractor_2_c_out), .A(A[2]), .B(B[2]), .Out(Out[2]), .C_out(n1_bit_subtractor_3_c_out));
  _1_Bit_Subtractor u_1_bit_subtractor_4 (
    .C_in(C_in), .A(A[0]), .B(B[0]), .Out(Out[0]), .C_out(n1_bit_subtractor_4_c_out));
endmodule

module _16_Bit_Adder (
  input  C_in,
  input  [15:0] B,
  input  [15:0] A,
  output [15:0] Out,
  output C_out
);

  wire n4_bit_adder_2_c_out, n4_bit_adder_3_c_out, n4_bit_adder_4_c_out;

  _4_Bit_Adder u_4_bit_adder_1 (
    .Out(Out[15:12]), .C_in(n4_bit_adder_2_c_out), .C_out(C_out), .B(B[15:12]), .A(A[15:12]));
  _4_Bit_Adder u_4_bit_adder_2 (
    .Out(Out[11:8]), .C_in(n4_bit_adder_3_c_out), .C_out(n4_bit_adder_2_c_out), .B(B[11:8]), .A(A[11:8]));
  _4_Bit_Adder u_4_bit_adder_3 (
    .Out(Out[7:4]), .C_in(n4_bit_adder_4_c_out), .C_out(n4_bit_adder_3_c_out), .B(B[7:4]), .A(A[7:4]));
  _4_Bit_Adder u_4_bit_adder_4 (.Out(Out[3:0]), .C_in(C_in), .C_out(n4_bit_adder_4_c_out), .B(B[3:0]), .A(A[3:0]));
endmodule

module _16_Bit_Subtractor (
  input  C_in,
  input  [15:0] B,
  input  [15:0] A,
  output [15:0] Out,
  output C_out
);

  wire n4_bit_subtractor_2_c_out, n4_bit_subtractor_3_c_out, n4_bit_subtractor_4_c_out;

  _4_Bit_Subtractor u_4_bit_subtractor_1 (
    .Out(Out[15:12]), .A(A[15:12]), .B(B[15:12]), .C_out(C_out), .C_in(n4_bit_subtractor_2_c_out));
  _4_Bit_Subtractor u_4_bit_subtractor_2 (
    .Out(Out[11:8]), .A(A[11:8]), .B(B[11:8]), .C_out(n4_bit_subtractor_2_c_out),
    .C_in(n4_bit_subtractor_3_c_out));
  _4_Bit_Subtractor u_4_bit_subtractor_3 (
    .Out(Out[7:4]), .A(A[7:4]), .B(B[7:4]), .C_out(n4_bit_subtractor_3_c_out),
    .C_in(n4_bit_subtractor_4_c_out));
  _4_Bit_Subtractor u_4_bit_subtractor_4 (
    .Out(Out[3:0]), .A(A[3:0]), .B(B[3:0]), .C_out(n4_bit_subtractor_4_c_out), .C_in(C_in));
endmodule

module _16_Bit_ALU (
  input  [15:0] A,
  input  C_in,
  input  [15:0] B,
  input  C_in_2,
  input  C_in_3,
  input  S2,
  input  S1,
  input  S0,
  output C_out,
  output C_out_2,
  output C_out_3,
  output [15:0] Out
);

  wire [15:0] and_1_out, n16_bit_adder_1_out, n16_bit_adder_2_out, n16_bit_subtractor_1_out, not_1_out,
       or_1_out, xor_1_out;

  _16_Bit_Adder u_16_bit_adder_1 (.Out(n16_bit_adder_1_out), .C_out(C_out), .C_in(C_in), .B(B), .A(A));
  _16_Bit_Subtractor u_16_bit_subtractor_1 (
    .A(A), .B(B), .Out(n16_bit_subtractor_1_out), .C_out(C_out_2), .C_in(C_in_2));
  _16_Bit_Adder u_16_bit_adder_2 (.Out(n16_bit_adder_2_out), .C_out(C_out_3), .C_in(C_in_3), .B(16'h1), .A(A));
  assign not_1_out = ~A;  // NOT_Gate not_1, 16 bits wide
  assign and_1_out = A & B;  // AND_Gate and_1, 16 bits wide
  assign or_1_out = A | B;  // OR_Gate or_1, 16 bits wide
  assign xor_1_out = A ^ B;  // XOR_Gate xor_1, 16 bits wide
  Multiplexer #(.select(3), .width(16), .disabled(0), .enable("false")) multiplexer_1 (
    .in0(n16_bit_adder_1_out), .in1(n16_bit_subtractor_1_out), .in2(n16_bit_adder_2_out), .in3(not_1_out),
    .in4({1'b0, A[15:1]}), .in5(and_1_out), .in6(or_1_out), .in7(xor_1_out), .out(Out), .sel({S2, S1, S0}));

  // Notes on the sheet:
  //   1. Addition
  //   2. Subtraction
  //   3. Increment
  //   4. Negation
  //   5. Bit Shift
  //   6. AND
  //   7. OR
  //   8. XOR
endmodule
