// Logisim project lab4.circ as structural Verilog: 4 circuits, main circuit demorgans
module demorgans (
  input  in_1,
  input  in_2,
  output out_3,
  output out_4
);

  wire and_1_out;

  or or_1 (out_3, in_1, in_2);
  and and_1 (and_1_out, ~in_1, ~in_2);  // AND_Gate
  not not_1 (out_4, and_1_out);

  // Other names for the same wires on the sheet: A = in_1; B = in_2; U = out_3; V = out_4

  // Notes on the sheet:
  //   Susan Roberts
  //   Lab 4
  //   9/3/14
endmodule

module NAND (
  input  A,
  input  B,
  output Q
);

  wire transistor_4_out;

  Transistor transistor_1 (.in(1'b1), .out(Q), .gate(A));
  Transistor #(.gate("br")) transistor_2 (.in(1'b1), .out(Q), .gate(B));
  Transistor #(.\type ("n")) transistor_3 (.in(transistor_4_out), .out(Q), .gate(A));
  Transistor #(.\type ("n")) transistor_4 (.in(1'b0), .out(transistor_4_out), .gate(B));

  // Notes on the sheet:
  //   Susan Roberts
  //   Lab 4
  //   9/3/14
endmodule

module NOT (
  input  A,
  output Q
);

  Transistor transistor_1 (.in(1'b1), .out(Q), .gate(A));
  Transistor #(.\type ("n")) transistor_2 (.in(1'b0), .out(Q), .gate(A));

  // Notes on the sheet:
  //   Susan Roberts
  //   Lab 4
  //   9/3/14
endmodule

module AND (
  input  A,
  input  B,
  output Q
);

  wire transistor_1_out, transistor_4_out;

  Transistor #(.gate("br")) transistor_1 (.in(1'b1), .out(transistor_1_out), .gate(B));
  Transistor transistor_2 (.in(1'b1), .out(transistor_1_out), .gate(A));
  Transistor #(.\type ("n")) transistor_3 (.in(transistor_4_out), .out(transistor_1_out), .gate(A));
  Transistor #(.\type ("n")) transistor_4 (.in(1'b0), .out(transistor_4_out), .gate(B));
  Transistor transistor_5 (.in(1'b1), .out(Q), .gate(transistor_1_out));
  Transistor #(.\type ("n")) transistor_6 (.in(1'b0), .out(Q), .gate(transistor_1_out));

  // Notes on the sheet:
  //   Susan Roberts
  //   Lab 4
  //   9/3/14
endmodule
