// Logisim project lab5.circ as structural Verilog: 3 circuits, main circuit Easy
module Easy (
  input  A,
  input  B,
  input  C,
  output out_4
);

  wire and_1_out, and_2_out;

  and and_1 (and_1_out, A, ~B);  // AND_Gate
  and and_2 (and_2_out, B, C);
  or or_1 (out_4, and_1_out, and_2_out);
endmodule

module Medium (
  input  A,
  input  B,
  input  C,
  output out_4
);

  wire and_1_out, and_2_out;

  and and_1 (and_1_out, B, C);
  and and_2 (and_2_out, ~B, ~C);  // AND_Gate
  or or_1 (out_4, A, and_1_out, and_2_out);
endmodule

module Hard (
  input  A,
  input  B,
  input  C,
  input  D,
  output out_5
);

  wire and_1_out, and_2_out, and_3_out, and_4_out;

  and and_1 (and_1_out, A, ~B);  // AND_Gate
  and and_2 (and_2_out, ~B, ~D);  // AND_Gate
  and and_3 (and_3_out, ~A, C, ~D);  // AND_Gate
  and and_4 (and_4_out, A, ~C, ~D);  // AND_Gate
  or or_1 (out_5, and_1_out, and_2_out, and_3_out, and_4_out);
endmodule
